# Fritzing sketch tp-led-ldr-montage (saved by Fritzing 0.9.4)
breadboards: 1

parts:
  WeMos_D1_Mini1 = WeMos D1 Mini
  LED1 = LED - 5mm [color="Red (633nm)" package="5 mm [THT]"]
  R1 = Resistor [tolerance=±5% resistance=220 package=THT]
  R2 = Resistor [tolerance=±5% resistance=220 package=THT]
  R3 = Photocell (LDR) [package=THT]

nets:
  N1: WeMos_D1_Mini1.A0, R2.Pin_1, R3.pin_1
  N2: WeMos_D1_Mini1.D1, R1.Pin_0
  N3: LED1.cathode, R2.Pin_0
  N4: LED1.anode, R1.Pin_1
  5V: R3.pin_0
