# Fritzing sketch tp4-montage (saved by Fritzing 0.9.4)
breadboards: 1

parts:
  R2 = Resistor [tolerance=±5% resistance=220 package=THT]
  R3 = Photocell (LDR) [package=THT]
  WeMos_D1_Mini1 = WeMos D1 Mini

nets:
  N1: R2.Pin_1, R3.pin_1, WeMos_D1_Mini1.A0
  5V: R3.pin_0
