# Fritzing sketch tp5-feu-montage (saved by Fritzing 0.9.4)
breadboards: 1

parts:
  WeMos_D1_Mini1 = WeMos D1 Mini
  LED1 = LED - 5mm [color="Red (633nm)" package="5 mm [THT]"]
  R1 = Resistor [tolerance=±5% resistance=220 package=THT]
  R3 = Photocell (LDR) [package=THT]
  R4 = Resistor [tolerance=±5% resistance=220 package=THT]
  R5 = Resistor [tolerance=±5% resistance=220 package=THT]
  LED2 = LED - 5mm [color="Orange (620nm)" package="5 mm [THT]"]
  LED3 = LED - 5mm [color="Green (570nm)" package="5 mm [THT]"]
  R2 = Resistor [tolerance=±5% resistance=220 package=THT]

nets:
  N1: WeMos_D1_Mini1.A0, R3.pin_1, R2.Pin_1
  N2: WeMos_D1_Mini1.D0, R5.Pin_0
  N3: WeMos_D1_Mini1.D5, R4.Pin_0
  N4: WeMos_D1_Mini1.D6, R1.Pin_0
  GND: LED1.cathode, LED2.cathode, LED3.cathode, R2.Pin_0
  N5: LED1.anode, R1.Pin_1
  N6: R4.Pin_1, LED2.anode
  N7: R5.Pin_1, LED3.anode
