# Fritzing sketch tp5-montage (saved by Fritzing 0.9.4)
breadboards: 1

parts:
  R2 = Resistor [tolerance=±5% resistance=3.3k package=THT]
  R1 = Photocell (LDR) [package=THT]
  part = WeMos D1 Mini

nets:
  N1: R2.Pin_1, R1.pin_1, part.A0
  5V: R1.pin_0
