# Fritzing sketch tp6-montage (saved by Fritzing 0.9.4)
breadboards: 1

parts:
  part = WeMos D1 Mini
  LED1 = LED - 5mm [color="Red (633nm)" package="5 mm [THT]"]
  R3 = Resistor [tolerance=±5% resistance=220 package=THT]
  R2 = Resistor [tolerance=±5% resistance=3.3k package=THT]
  R1 = Photocell (LDR) [package=THT]

nets:
  N1: part.A0, R2.Pin_1, R1.pin_1
  N2: part.D1, R3.Pin_0
  N3: LED1.cathode, R2.Pin_0
  N4: LED1.anode, R3.Pin_1
  5V: R1.pin_0
