# Fritzing sketch tp8.1-montage (saved by Fritzing 0.9.4)
breadboards: 1

parts:
  WeMos_D1_Mini1 = WeMos D1 Mini
  HC-SR04_Sensor_1 = HC-SR04 Ultrasonic Distance Sensor

nets:
  N1: WeMos_D1_Mini1.D1, HC-SR04_Sensor_1.ECHO
  N2: WeMos_D1_Mini1.D2, HC-SR04_Sensor_1.TRIG
  5V: HC-SR04_Sensor_1.VCC
  GND: HC-SR04_Sensor_1.GND

custom parts:
  HC-SR04 Ultrasonic Distance Sensor: The HC-SR04 is an ultrasonic distance sensor. It is capable of providing measurement for ranges of 2cm to 400cm. The module operates at 5V.
