# Fritzing sketch tp8.2-montage (saved by Fritzing 0.9.4)
breadboards: 1

parts:
  WeMos_D1_Mini1 = WeMos D1 Mini
  LED1 = LED - 5mm [color="Red (633nm)" package="5 mm [THT]"]
  LED3 = LED - 5mm [color="Green (570nm)" package="5 mm [THT]"]
  R4 = Resistor [tolerance=±5% resistance=220 package=THT]
  LED2 = LED - 5mm [color="Orange (620nm)" package="5 mm [THT]"]
  R5 = Resistor [tolerance=±5% resistance=220 package=THT]
  HC-SR04_Sensor_1 = HC-SR04 Ultrasonic Distance Sensor
  R6 = Resistor [tolerance=±5% resistance=220 package=THT]

nets:
  N1: WeMos_D1_Mini1.D1, HC-SR04_Sensor_1.ECHO
  N2: WeMos_D1_Mini1.D2, HC-SR04_Sensor_1.TRIG
  N3: WeMos_D1_Mini1.D6, R4.Pin_0
  GND: LED1.cathode, LED3.cathode, LED2.cathode, HC-SR04_Sensor_1.GND
  N4: LED1.anode, R6.Pin_1
  N5: LED3.anode, R4.Pin_1
  N6: LED2.anode, R5.Pin_1
  5V: HC-SR04_Sensor_1.VCC

custom parts:
  HC-SR04 Ultrasonic Distance Sensor: The HC-SR04 is an ultrasonic distance sensor. It is capable of providing measurement for ranges of 2cm to 400cm. The module operates at 5V.
